# Fritzing sketch ArduinoMinimal_TestIPv4 (saved by Fritzing 0.9.3b)
circuit board: 4.8cm x 5.3cm

parts:
  U1 = atmega328 [package=dip]
  R1 = Resistor [tolerance=±5% resistance=10k package=THT]
  XTAL1 = Crystal [frequency="16 Mhz" package=THT]
  C1 = Ceramic Capacitor [capacitance=1p package="100 mil [THT, multilayer]"]
  C2 = Ceramic Capacitor [capacitance=100nF package="100 mil [THT, multilayer]"]
  Componente2 = Arduino Uno (Rev3)

nets:
  N1: U1.RESET, R1.Pin_0, Componente2.RESET
  N2: U1.D0_(RX), Componente2.D0/RX
  N3: U1.D1_(TX), Componente2.D1/TX
  N4: U1.D2, Componente2.D2
  N5: U1.D3_(PWM), Componente2.D3_PWM
  N6: U1.D4, Componente2.D4
  VCC: U1.VCC, U1.AVCC, R1.Pin_1, Componente2.5V
  GND: U1.GND, C1.0, C2.1, Componente2.GND
  N7: U1.XLAT1, XTAL1.pin_1, C2.0
  N8: U1.XLAT2, XTAL1.pin_0, C1.1
  N9: U1.D5_(PWM), Componente2.D5_PWM
  N10: U1.D6_(PWM), Componente2.D6_PWM
  N11: U1.D7, Componente2.D7
  N12: U1.D8, Componente2.D8
  N13: U1.D9_(PWM), Componente2.D9_PWM
  N14: U1.D10_(PWM), Componente2.D10_PWM/SS
  N15: U1.D11_(PWM), Componente2.D11_PWM/MOSI
  N16: U1.D12, Componente2.D12/MISO
  N17: U1.D13, Componente2.D13/SCK
  N18: U1.A0, Componente2.A0
  N19: U1.A1, Componente2.A1
  N20: U1.A2, Componente2.A2
  N21: U1.A3, Componente2.A3
  N22: U1.A4, Componente2.A4/SDA
  N23: U1.A5, Componente2.A5/SCL

notes:
  BOTTOM
  Atmega328
  Arduino
  Minimal
  Designed for
  Test-Ethernet-IPv4
